# Fritzing sketch circuito (saved by Fritzing 0.9.6b)
breadboards: 1

parts:
  U1 = LCD-16X2 [package=lcd-16x2]
  Componente2 = Thumb Joystick
  HC-SR04_Sensor_1 = HC-SR04 Ultrasonic Distance Sensor
  S2 = Pushbutton [package="[THT]"]
  LED1 = smd LED [color="Red (633nm)" package="0603 [SMD]"]
  LED2 = smd LED [color="Green (565nm)" package="0603 [SMD]"]
  Mod1 = KY-015 Temperature & Humidity Sensor Module [package="Breakout board"]
  Componente4 = Arduino Uno (Rev3) - ICSP
  R1 = Resistor [tolerance=±5% resistance=1k package="0805 [SMD]"]
  R3 = Resistor [tolerance=±5% resistance=330k package="0805 [SMD]"]
  R4 = Resistor [tolerance=±5% resistance=330k package="0805 [SMD]"]

nets:
  GND: U1.VSS, U1.VO, U1.R_W, U1.K, Componente2.GND, HC-SR04_Sensor_1.GND, S2.Pin_1, S2.Pin_2, Mod1.-, Componente4.GND, R3.Pin_0, R4.Pin_0
  VCC: U1.VDD, Componente2.VCC, HC-SR04_Sensor_1.VCC, Mod1.Vin, Componente4.5V, R1.Pin_1
  N1: U1.RS, Componente4.D12/MISO
  N2: U1.E, Componente4.D11_PWM/MOSI
  N3: U1.DB4, Componente4.D5_PWM
  N4: U1.DB5, Componente4.D4
  N5: U1.DB6, Componente4.D3_PWM
  N6: U1.DB7, Componente4.D2
  N7: U1.A, R1.Pin_0
  N8: Componente2.SEL, Componente4.D13/SCK
  N9: Componente2.HORZ, Componente4.A5/SCL
  N10: Componente2.VERT, Componente4.A4/SDA
  N11: HC-SR04_Sensor_1.TRIG, Componente4.D7
  N12: HC-SR04_Sensor_1.ECHO, Componente4.D8
  N13: S2.Pin_3, S2.Pin_4, Componente4.D10_PWM/SS
  N14: LED1.cathode, R4.Pin_1
  N15: LED1.anode, Componente4.D6_PWM
  N16: LED2.cathode, R3.Pin_1
  N17: LED2.anode, Componente4.A2
  N18: Mod1.S, Componente4.D9_PWM

custom parts:
  KY-015 Temperature & Humidity Sensor Module: KY-015 temperature and humidity sensor module, provides a low-latency serial interface to measure humidity and temperature.
